# Fritzing sketch falko_business.card (saved by Fritzing 0.9.3b)
circuit board: 8.5cm x 5.5cm
breadboards: 1

parts:
  S1 = Pushbutton [package="[THT]"]
  R1 = Resistor [tolerance=±5% resistance=220 package=THT]
  LED1 = LED - 5mm [color="Red (633nm)" package="5 mm [THT]"]
  VCC1 = Battery
  D1 = Rectifier Diode [part_number=1N4001 package="300 mil [THT]"]
  D2 = Rectifier Diode [part_number=1N4001 package="300 mil [THT]"]
  D3 = Rectifier Diode [part_number=1N4001 package="300 mil [THT]"]
  D4 = Rectifier Diode [part_number=1N4001 package="300 mil [THT]"]
  IOT = Pad [width=2 height=2 connect=center]
  DATA = Pad [width=2 height=2 connect=center]
  MOBILITY = Pad [width=2 height=2 connect=center]
  Pad4 = Pad [width=2 height=2 connect=center]

nets:
  N1: S1.Pin_1, S1.Pin_2, R1.Pin_0
  N2: S1.Pin_3, VCC1.+
  N3: R1.Pin_1, LED1.anode
  N4: LED1.cathode, VCC1.-
  N5: D1.cathode, D2.cathode
  N6: D1.anode, D4.anode
  N7: D2.anode, D3.anode
  N8: D3.cathode, D4.cathode
  N9: IOT.pad, DATA.pad, MOBILITY.pad, Pad4.pad

notes:
  falko@urbandrivestyle.com
  head of technology
  +49 1515 740 1235
  Urban Drivestyle | why.taxi
